# Fritzing sketch avrmodem (saved by Fritzing 0.9.5d)

parts:
  Part1 = Arduino Mega 2560 (Rev3)
  J1 = Piezo Speaker
  LED2 = smd LED [color="Green (570nm)" package="0603 [SMD]"]
  Nokia_5110_LCD_Module2 = Nokia 5110 LCD basado en PCD8544
  LED1 = smd LED [color="Red (633nm)" package="0603 [SMD]"]

nets:
  N1: Part1.GND, J1.pin1, LED2.cathode, Nokia_5110_LCD_Module2.SCLK, Nokia_5110_LCD_Module2.LED, LED1.cathode
  N2: Part1.D11_PWM, J1.pin2
  N3: Part1.3V3, Nokia_5110_LCD_Module2.DN(MODI)
  N4: Part1.D3_PWM, Nokia_5110_LCD_Module2.VCC
  N5: Part1.D4_PWM, Nokia_5110_LCD_Module2.GND
  N6: Part1.D5_PWM, Nokia_5110_LCD_Module2.SCE
  N7: Part1.D31, LED1.anode
  N8: Part1.D51, Nokia_5110_LCD_Module2.RST
  N9: Part1.D52, Nokia_5110_LCD_Module2.D/C
  N10: Part1.D53, LED2.anode

custom parts:
  Nokia 5110 LCD basado en PCD8544: Módulo Nokia 5110 LCD basado en el controlador PCD8544. Versión de 8 pines (sólo entrada).
